# Fritzing sketch fritzing_diagram (saved by Fritzing 0.9.5d)

parts:
  Part1 = Itsy Bitsy 32u4 5V @ 16MHz [part_number="Adafruit #3677"]
  S1 = Round Pushbutton
  DIN1 = DIN-5 jack (MIDI) [package=THT]
  J1 = Power Jack [package=power_jack_slot]
  R1 = Resistor [tolerance=±5% resistance=220 package=THT]
  R2 = Resistor [tolerance=±5% resistance=220 package=THT]
  S2 = Round Pushbutton
  S3 = Round Pushbutton
  S4 = Round Pushbutton
  Part2 = Adafruit Breadboard-Friendly NeoPixel [part_number="Adafruit #1312"]
  Part3 = Adafruit Breadboard-Friendly NeoPixel [part_number="Adafruit #1312"]
  Part4 = Adafruit Breadboard-Friendly NeoPixel [part_number="Adafruit #1312"]
  Part5 = Adafruit Breadboard-Friendly NeoPixel [part_number="Adafruit #1312"]

nets:
  N1: Part1.D4, S1.leg0
  N2: Part1.VBAT, J1.GNDBREAK
  GND: Part1.GND, DIN1.2, J1.GND, Part2.GND, Part3.GND, Part4.GND, Part5.GND
  N3: Part1.D10, Part2.IN
  N4: Part1.D9, S4.leg0
  N5: Part1.D7, S3.leg0
  N6: Part1.D5, S2.leg0
  N7: Part1.D1, R1.Pin_1
  VDD: Part1.+5V, R2.Pin_1, Part2.VDD, Part3.VDD, Part4.VDD, Part5.VDD
  N8: S1.leg1, S2.leg1, S3.leg1, S4.leg1
  N9: DIN1.5, R1.Pin_0
  N10: DIN1.4, R2.Pin_0
  N11: Part2.OUT, Part4.IN
  N12: Part3.IN, Part5.OUT
  N13: Part4.OUT, Part5.IN

notes:
  Button1
  Button2
  Button3
  Button4

custom parts:
  Itsy Bitsy 32u4 5V @ 16MHz: What's smaller than a Feather but larger than a Trinket? It's an Itsy Bitsy! Small, powerful, Arduino-compatible - this microcontroller board is perfect when you want something very compact, but still with a bunch of pins. Itsy Bitsy is only 1.4" long by 0.7" wide, but has 6 power pins, 6 analog & digital pins and 17 digital pins. It packs much of the same capability as an Arduino UNO. So it's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
  Adafruit Breadboard-Friendly NeoPixel: This is the easiest way possible to add small, bright RGB pixels to your project. We took the same technology from our Flora NeoPixels and made them breadboard friendly, with two rows of 3 x 0.1" spaced header on each side for easy soldering, chaining and breadboarding. These ultra-bright LEDs have a constant-current driver cooked right into the LED package! The pixels are chainable - so you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
